# Fritzing sketch board (saved by Fritzing 0.9.3b)
breadboards: 2

parts:
  Pro_Micro1 = SparkFun Pro Micro
  R1 = Resistor [tolerance=±5% resistance=1k package=THT]
  S1 = Toggle Switch spst [package=THT]
  R2 = Resistor [tolerance=±5% resistance=1k package=THT]
  LED1 = LED - 5mm [color="Red (633nm)" package="5 mm [THT]"]

nets:
  N1: Pro_Micro1.GND, S1.L1, LED1.cathode
  N2: Pro_Micro1.5, R2.Pin_1
  N3: Pro_Micro1.15, R1.Pin_0, S1.COM
  N4: Pro_Micro1.RAW, R1.Pin_1
  N5: R2.Pin_0, LED1.anode

custom parts:
  SparkFun Pro Micro: The Pro Micro is similar to the Pro Mini except with an ATmega32U4 on board. The USB transceiver inside the 32U4 allows us to add USB connectivity on-board and do away with bulky external USB interface. Based on: https://github.com/unorthodox-engineers/unorthodox-arduino/blob/master/Unorthodox/fritzing/parts/Pro%20Micro.fzpz
  Toggle Switch spst: Toggle Switch single pole single throw
